# Fritzing sketch schematic (saved by Fritzing 0.7.4b)

parts:
  Arduino1 = Arduino
  R1 = Resistor [tolerance=±5% resistance=220 package=THT]
  D1 = Rectifier Diode [part_number=1N4001 package="300 mil [THT]"]
  K1 = Relay [part_number=FRS1B-S package=THT]
  Q1 = NPN-Transistor [package="TO92 [THT]"]

nets:
  N1: Arduino1.GND, Q1.E
  N2: Arduino1.D12, R1.Pin_1
  N3: Arduino1.VIN, D1.cathode, K1.COIL1
  N4: D1.anode, K1.COIL2, Q1.C
